// Logisim project Proyecto Divisio╠ün Binaria (Logisim).circ as structural Verilog: 2 circuits, main circuit main
module main (
  input  Dividendo,
  input  in_2,
  input  in_3,
  input  Divisor,
  input  in_5,
  input  in_6
);

  wire and_1_out, and_2_out, and_3_out, and_4_out, and_5_out, and_6_out, and_7_out, and_8_out, and_9_out,
       and_10_out, and_11_out, and_12_out, and_13_out, and_14_out, and_15_out, and_16_out, and_17_out,
       and_18_out, and_19_out, and_20_out, and_21_out, and_22_out, and_23_out, and_24_out, and_25_out,
       and_26_out, and_27_out, and_28_out, and_29_out, and_30_out, and_31_out, and_32_out, and_33_out,
       and_34_out, and_35_out, and_36_out, and_37_out, and_38_out, and_39_out, and_40_out, and_41_out,
       and_42_out, and_43_out, and_44_out, and_45_out, and_46_out, and_47_out, and_48_out, and_49_out,
       and_50_out, and_51_out, and_52_out, and_53_out, and_54_out, and_55_out, and_56_out, and_57_out,
       and_58_out, and_59_out, and_60_out, and_61_out, and_62_out, and_63_out, and_64_out, and_65_out,
       and_66_out, and_67_out, and_68_out, and_69_out, and_70_out, and_71_out, and_72_out, and_73_out,
       and_74_out, and_75_out, and_76_out, and_77_out, and_78_out, and_79_out, and_80_out, and_81_out,
       and_82_out, and_83_out, and_84_out, and_85_out, and_86_out, and_87_out, and_88_out, and_89_out,
       and_90_out, and_91_out, and_92_out, and_93_out, and_94_out, and_95_out, and_96_out, and_97_out,
       and_98_out, and_99_out, and_100_out, and_101_out, and_102_out, and_103_out, and_104_out, and_105_out,
       and_106_out, and_107_out, and_108_out, and_109_out, and_110_out, and_111_out, and_112_out,
       and_113_out, and_114_out, and_115_out, not_1_out, not_2_out, not_3_out, not_4_out, not_5_out,
       not_6_out, or_1_out, or_2_out, or_3_out, or_4_out, or_5_out, or_6_out, or_7_out, or_8_out, or_9_out,
       or_10_out, or_11_out, or_12_out, or_13_out, or_14_out, or_15_out;

  and and_1 (and_1_out, Dividendo, or_1_out, not_6_out, in_6);
  _7_Segment_Display u_7_segment_display_1 (.b(and_1_out), .c(and_1_out));  // open: g, f, a, e, d, dp
  _7_Segment_Display u_7_segment_display_2 (
    .g(or_5_out), .f(or_7_out), .a(or_13_out), .b(or_15_out), .e(or_10_out), .d(or_12_out), .c(or_14_out));  // open: dp
  not not_1 (not_1_out, Divisor);
  not not_2 (not_2_out, in_3);
  not not_3 (not_3_out, in_2);
  not not_4 (not_4_out, Dividendo);
  not not_5 (not_5_out, in_6);
  not not_6 (not_6_out, in_5);
  or or_1 (or_1_out, in_3, in_2);
  _7_Segment_Display u_7_segment_display_3 (
    .g(or_11_out), .f(or_9_out), .a(or_2_out), .b(or_3_out), .e(or_8_out), .d(or_6_out), .c(or_4_out));  // open: dp
  and and_2 (and_2_out, not_6_out, in_6);
  and and_3 (and_3_out, not_1_out, in_5, not_5_out);
  and and_4 (and_4_out, not_4_out, not_3_out, not_1_out, in_6);
  and and_5 (and_5_out, not_4_out, not_3_out, in_3, in_6);
  and and_6 (and_6_out, in_2, in_3, not_1_out, in_6);
  and and_7 (and_7_out, Dividendo, not_3_out, not_2_out, in_6);
  and and_8 (and_8_out, Dividendo, not_2_out, not_1_out, in_6);
  and and_9 (and_9_out, Dividendo, in_3, Divisor, in_6);
  and and_10 (and_10_out, not_4_out, in_2, not_2_out, Divisor, in_6);
  or or_2 (or_2_out, and_2_out, and_3_out, and_4_out, and_5_out, and_6_out, and_7_out, and_8_out, and_9_out, and_10_out);
  or or_3 (or_3_out, not_4_out, Dividendo);
  and and_11 (and_11_out, not_2_out, not_3_out, not_4_out);
  and and_12 (and_12_out, Divisor, not_3_out, not_4_out);
  and and_13 (and_13_out, not_1_out, in_2, not_4_out);
  and and_14 (and_14_out, not_1_out, not_2_out, in_2);
  and and_15 (and_15_out, Divisor, in_3, in_2);
  and and_16 (and_16_out, Divisor, not_2_out, Dividendo);
  and and_17 (and_17_out, Dividendo, not_3_out, in_3, not_1_out);
  or or_4 (or_4_out, not_5_out, not_6_out, and_11_out, and_12_out, and_13_out, and_14_out, and_15_out, and_16_out, and_17_out);
  or or_5 (or_5_out, and_18_out, and_19_out, and_20_out, and_21_out, and_22_out, and_23_out, and_24_out, and_25_out, and_26_out);
  and and_18 (and_18_out, not_5_out, not_6_out);
  and and_19 (and_19_out, Dividendo, not_2_out);
  and and_20 (and_20_out, Dividendo, not_3_out, in_5);
  and and_21 (and_21_out, not_4_out, in_2, not_5_out);
  and and_22 (and_22_out, in_2, not_1_out, not_6_out);
  and and_23 (and_23_out, Dividendo, in_2, in_6);
  and and_24 (and_24_out, in_2, not_2_out, not_6_out);
  and and_25 (and_25_out, not_4_out, not_3_out, in_3, not_6_out);
  and and_26 (and_26_out, in_2, in_3, in_5, in_6);
  and and_27 (and_27_out, not_5_out, not_1_out);
  and and_28 (and_28_out, not_1_out, not_3_out, not_4_out);
  and and_29 (and_29_out, not_1_out, in_3, in_2);
  and and_30 (and_30_out, not_1_out, not_2_out, Dividendo);
  and and_31 (and_31_out, in_6, in_3, not_3_out, not_4_out);
  and and_32 (and_32_out, in_6, not_2_out, not_3_out, Dividendo);
  and and_33 (and_33_out, in_6, Divisor, in_3, Dividendo);
  and and_34 (and_34_out, in_6, Divisor, not_2_out, in_2, not_4_out);
  or or_6 (or_6_out, not_6_out, and_27_out, and_28_out, and_29_out, and_30_out, and_31_out, and_32_out, and_33_out, and_34_out);
  and and_35 (and_35_out, not_5_out, not_1_out);
  and and_36 (and_36_out, not_1_out, not_3_out, not_4_out);
  and and_37 (and_37_out, not_1_out, in_3, in_2);
  and and_38 (and_38_out, not_1_out, not_2_out, Dividendo);
  and and_39 (and_39_out, in_6, in_3, not_3_out, not_4_out);
  and and_40 (and_40_out, in_6, not_2_out, not_3_out, Dividendo);
  and and_41 (and_41_out, in_6, Divisor, in_3, Dividendo);
  and and_42 (and_42_out, in_6, Divisor, not_2_out, in_2, not_4_out);
  or or_7 (or_7_out, and_43_out, and_44_out, and_45_out, and_46_out, and_47_out, and_48_out, and_49_out, and_50_out, and_51_out, and_52_out);
  or or_8 (or_8_out, not_6_out, and_35_out, and_36_out, and_37_out, and_38_out, and_39_out, and_40_out, and_41_out, and_42_out);
  and and_43 (and_43_out, not_4_out, not_3_out, not_2_out, in_5);
  and and_44 (and_44_out, Dividendo, not_3_out, in_5, not_5_out);
  and and_45 (and_45_out, Dividendo, in_2, not_2_out, in_5);
  and and_46 (and_46_out, Dividendo, in_2, in_3, in_6);
  and and_47 (and_47_out, not_4_out, not_3_out, not_2_out, not_1_out, in_6);
  and and_48 (and_48_out, not_4_out, not_3_out, not_1_out, in_5, in_6);
  and and_49 (and_49_out, not_4_out, in_2, not_2_out, not_6_out, in_6);
  and and_50 (and_50_out, not_4_out, in_2, not_1_out, not_6_out, in_6);
  and and_51 (and_51_out, Dividendo, not_3_out, not_2_out, not_6_out, in_6);
  and and_52 (and_52_out, Dividendo, not_3_out, not_1_out, not_6_out, in_6);
  and and_53 (and_53_out, in_6, not_6_out);
  and and_54 (and_54_out, not_5_out, in_5, not_1_out);
  and and_55 (and_55_out, in_6, not_1_out, not_2_out, not_3_out, not_4_out);
  and and_56 (and_56_out, in_6, Divisor, in_3, not_3_out, not_4_out);
  and and_57 (and_57_out, in_6, not_1_out, in_3, in_2, not_4_out);
  and and_58 (and_58_out, in_6, Divisor, not_2_out, not_3_out, Dividendo);
  and and_59 (and_59_out, in_6, not_1_out, not_2_out, in_2, Dividendo);
  and and_60 (and_60_out, in_6, Divisor, in_3, in_2, Dividendo);
  or or_9 (or_9_out, and_53_out, and_54_out, and_55_out, and_56_out, and_57_out, and_58_out, and_59_out, and_60_out);
  or or_10 (or_10_out, and_61_out, and_62_out, and_63_out, and_64_out, and_65_out, and_66_out, and_67_out, and_68_out);
  and and_61 (and_61_out, not_5_out, not_6_out);
  and and_62 (and_62_out, not_3_out, not_1_out, not_6_out);
  and and_63 (and_63_out, in_2, not_2_out, not_5_out);
  and and_64 (and_64_out, not_3_out, not_2_out, not_1_out, in_6);
  and and_65 (and_65_out, not_4_out, in_3, not_1_out, in_6);
  and and_66 (and_66_out, not_4_out, not_3_out, not_2_out, in_5);
  and and_67 (and_67_out, Dividendo, not_2_out, not_1_out, not_6_out);
  and and_68 (and_68_out, not_4_out, in_3, in_2, in_5, in_6);
  and and_69 (and_69_out, not_5_out, not_6_out);
  and and_70 (and_70_out, in_6, in_5, not_1_out, in_3, not_3_out, not_4_out);
  and and_71 (and_71_out, in_6, in_5, Divisor, not_2_out, in_2, not_4_out);
  and and_72 (and_72_out, in_6, in_5, not_1_out, not_2_out, not_3_out, Dividendo);
  and and_73 (and_73_out, in_6, in_5, Divisor, in_3, not_3_out, Dividendo);
  and and_74 (and_74_out, in_6, in_5, not_1_out, in_3, in_2, Dividendo);
  or or_11 (or_11_out, and_69_out, and_70_out, and_71_out, and_72_out, and_73_out, and_74_out);
  or or_12 (or_12_out, and_75_out, and_76_out, and_77_out, and_78_out, and_79_out, and_80_out, and_81_out, and_82_out, and_83_out, and_84_out, and_85_out, and_86_out);
  and and_75 (and_75_out, not_6_out, not_5_out);
  and and_76 (and_76_out, not_4_out, not_2_out, not_5_out);
  and and_77 (and_77_out, in_2, not_2_out, not_5_out);
  and and_78 (and_78_out, not_3_out, not_1_out, in_6);
  and and_79 (and_79_out, Dividendo, not_2_out, not_1_out, not_6_out);
  and and_80 (and_80_out, not_3_out, not_2_out, in_5, in_6);
  and and_81 (and_81_out, not_4_out, in_2, in_3, not_1_out);
  and and_82 (and_82_out, not_4_out, not_3_out, in_3, not_6_out);
  and and_83 (and_83_out, in_2, not_2_out, Divisor, not_6_out);
  and and_84 (and_84_out, Dividendo, not_3_out, in_3, in_5);
  and and_85 (and_85_out, not_4_out, in_2, in_3, in_5);
  and and_86 (and_86_out, Dividendo, in_2, in_3, Divisor, in_6);
  and and_87 (and_87_out, in_5, in_3, not_3_out, Dividendo);
  and and_88 (and_88_out, in_6, not_6_out, not_2_out, Dividendo);
  and and_89 (and_89_out, in_6, Divisor, in_3, in_2);
  and and_90 (and_90_out, in_6, not_6_out, Divisor, in_2);
  and and_91 (and_91_out, in_6, not_6_out, in_3, not_4_out);
  and and_92 (and_92_out, in_6, not_1_out, in_3, not_4_out);
  and and_93 (and_93_out, in_6, in_5, not_2_out, not_3_out);
  and and_94 (and_94_out, in_5, not_2_out, not_3_out, not_4_out);
  and and_95 (and_95_out, not_5_out, in_5, in_2);
  and and_96 (and_96_out, in_6, not_1_out, not_3_out);
  or or_13 (or_13_out, and_87_out, and_88_out, and_89_out, and_90_out, and_91_out, and_92_out, and_93_out, and_94_out, and_95_out, and_96_out);
  or or_14 (or_14_out, and_106_out, and_107_out, and_108_out, and_109_out, and_110_out, and_111_out, and_112_out, and_113_out, and_114_out, and_115_out);
  and and_97 (and_97_out, not_5_out, in_3, in_2);
  and and_98 (and_98_out, Divisor, in_3, not_4_out);
  and and_99 (and_99_out, in_6, not_1_out, Dividendo);
  and and_100 (and_100_out, in_6, not_2_out, Dividendo);
  and and_101 (and_101_out, not_6_out, not_1_out, not_2_out);
  and and_102 (and_102_out, in_6, not_3_out);
  and and_103 (and_103_out, in_5, not_4_out);
  and and_104 (and_104_out, not_2_out, not_3_out);
  and and_105 (and_105_out, not_5_out, not_6_out);
  and and_106 (and_106_out, Dividendo, in_3);
  and and_107 (and_107_out, in_3, not_5_out);
  and and_108 (and_108_out, Divisor, not_6_out);
  and and_109 (and_109_out, Dividendo, not_5_out);
  and and_110 (and_110_out, not_3_out, Divisor);
  and and_111 (and_111_out, not_3_out, not_2_out, not_6_out);
  and and_112 (and_112_out, Dividendo, in_2, in_5);
  and and_113 (and_113_out, not_4_out, not_3_out, in_5);
  and and_114 (and_114_out, not_4_out, in_2, not_6_out);
  and and_115 (and_115_out, not_4_out, not_2_out, in_6);
  or or_15 (or_15_out, and_97_out, and_98_out, and_99_out, and_100_out, and_101_out, and_102_out, and_103_out, and_104_out, and_105_out);

  // Notes on the sheet:
  //   Cociente
  //   Cociente C
  //   Cociente D
  //   Cociente E
  //   Cociente F
  //   Cociente G
  //   Residuo
  //   Residuo E
  //   Residuo F
  //   Residuo G
  //   Cociente A
  //   Cociente B
  //   Residuo
  //   Residuo A
  //   Residuo B
  //   Residuo C
  //   Residuo D
  //   Cociente
endmodule

// qqqq
module Fisico (
  input  Dividendo,
  input  in_2,
  input  Divisor,
  input  in_4
);

  wire _1_out, _2_out, _3_out, _4_out, _5_out, _6_out, _7_out, _8_out, _9_out, _10_out, _11_out, _12_out,
       _13_out, _14_out, _15_out, _16_out, _17_out, _18_out, _19_out, not_1_out, not_2_out, not_3_out,
       not_4_out, or_1_out, or_2_out, or_3_out, or_4_out, or_5_out, or_6_out, or_7_out, or_8_out, or_9_out,
       or_10_out, or_11_out;

  not not_1 (not_1_out, Dividendo);
  not not_2 (not_2_out, in_2);
  not not_3 (not_3_out, Divisor);
  not not_4 (not_4_out, in_4);
  and _1 (_1_out, not_2_out, in_4);
  and _2 (_2_out, not_1_out, Divisor);
  and _3 (_3_out, Dividendo, not_3_out);
  or or_1 (or_1_out, Divisor, _5_out);
  and _5 (_5_out, not_1_out, in_4);
  and _6 (_6_out, in_2, in_4);
  and _7 (_7_out, not_2_out, in_4);
  and _8 (_8_out, not_1_out, Divisor);
  and _9 (_9_out, Dividendo, not_3_out);
  and _10 (_10_out, _9_out, in_4);
  and _11 (_11_out, not_2_out, in_4);
  and _12 (_12_out, not_1_out, Divisor);
  and _13 (_13_out, not_1_out, Divisor);
  and _14 (_14_out, not_1_out, not_2_out);
  and _15 (_15_out, _14_out, in_4);
  and _16 (_16_out, not_2_out, Divisor);
  and _17 (_17_out, _16_out, in_4);
  and _18 (_18_out, not_3_out, not_4_out);
  and _19 (_19_out, Dividendo, not_3_out);
  or or_2 (or_2_out, _1_out, _2_out);
  or or_3 (or_3_out, or_2_out, _4_out);
  and _4 (_4_out, _3_out, in_4);
  or or_4 (or_4_out, Divisor, in_4);
  or or_5 (or_5_out, or_1_out, _6_out);
  or or_6 (or_6_out, _7_out, _8_out);
  or or_7 (or_7_out, or_6_out, _10_out);
  or or_8 (or_8_out, _11_out, _12_out);
  or or_9 (or_9_out, _13_out, _15_out);
  or or_10 (or_10_out, _18_out, _19_out);
  _7_Segment_Display u_7_segment_display_1 (
    .g(or_10_out), .f(or_11_out), .a(or_3_out), .b(or_4_out), .e(or_8_out), .d(or_7_out), .c(or_5_out));  // open: dp
  or or_11 (or_11_out, or_9_out, _17_out);

  // Notes on the sheet:
  //   Segmento A
  //   Segmento B
  //   Segmento C
  //   Segmento D
  //   Segmento F
  //   Segmento G
  //   Segmento E
endmodule
